# Fritzing sketch fridge_circuit (saved by Fritzing 0.9.3b)
breadboards: 1

parts:
  Part1 = Arduino Uno (Rev3) - ICSP
  S1 = SWITCH-MOMENTARY-2 [package=reed_switch_plastic]
  10Kohm = Resistor [tolerance=±5% resistance=220 package="0603 [SMD]"]
  J1 = Piezo Speaker
  VCC1 = Battery block 9V
  S2 = Toggle Switch [package=THT]
  LED1 = LED - 5mm [color="Red (633nm)" package="5 mm [THT]"]
  R1 = Resistor [tolerance=±5% resistance=220 package=THT]
  S3 = SWITCH-MOMENTARY-2 [package=reed_switch_plastic]
  R2 = Resistor [tolerance=±5% resistance=220 package=THT]  # not connected
  LED2 = LED - 5mm [color="Green (555nm)" package="5 mm [THT]"]

nets:
  N1: Part1.GND, 10Kohm.Pin_0, J1.pin1, LED1.cathode, LED2.cathode
  N2: Part1.D8, S1.1, 10Kohm.Pin_1
  N3: Part1.D11_PWM/MOSI, J1.pin2, R1.Pin_0
  N4: S1.2, S3.1
  N5: VCC1.+, S2.L1
  N6: LED1.anode, R1.Pin_1
